# Fritzing sketch a3midifritzingboard (saved by Fritzing 0.9.3b)
stripboards: 1

parts:
  Teensy_3_1 = Teensy 3.1  # not connected
  IC2 = IC, DIP package, 6 pins [chip_label=PC900V]
  R5 = Resistor [tolerance=±5% resistance=270 package=THT]
  C2 = Electrolytic Capacitor [capacitance=10µF voltage=35V package="100 mil [THT, electrolytic]"]
  JP2 = RCA [package=rca_lock]
  C3 = Tantalum Capacitor [capacitance=1μF package="100 mil [THT, tantalum]"]
  U3 = MIDI_CONN_FEMALE [package=din_5_female]
  D2 = Diode [package=diode-1n4148]
  U4 = MIDI_CONN_FEMALE [package=din_5_female]
  R8 = Resistor [tolerance=±5% resistance=47 package=THT]
  S1 = Round Pushbutton
  R9 = Resistor [tolerance=±5% resistance=47 package=THT]
  R6 = Resistor [tolerance=±5% resistance=220 package=THT]

nets:
  N1: IC2.pin1, D2.A, R6.Pin_1
  N2: IC2.pin2, U3.MIDI_OUT, D2.C
  N3: IC2.pin4, R5.Pin_1
  N4: IC2.pin6, C3.+
  N5: R5.Pin_0, R9.Pin_0
  N6: C2.+, JP2.PIN
  N7: JP2.SHELL, C3.-, U4.NC2, S1.leg0
  N8: U3.MIDI_IN, R6.Pin_0
  N9: U4.MIDI_IN, R9.Pin_1
  N10: U4.MIDI_OUT, R8.Pin_0

notes:
  midi in
  midi out
  1 cables through plate
  2 usb to teensy -test
  3 components/wires to board
  4 teensy to board
